// Logisim project MIPS Single-Cycle Datapath With Control.circ as structural Verilog: 7 circuits, main circuit main
module main (
);

  wire alu_1_zero, and_1_out, clock_1_out, main_control_1_alusrc, main_control_1_branch, main_control_1_jump,
       main_control_1_memread, main_control_1_memtoreg, main_control_1_memwrite, main_control_1_regdst,
       main_control_1_regwrite, not_1_out, not_2_out;
  wire [1:0] main_control_1_aluop;
  wire [2:0] alu_control_1_operation;
  wire [4:0] multiplexer_1_out;
  wire [25:0] adder_1_out, adder_2_out, multiplexer_3_out, multiplexer_4_out, PC_q, shifter_1_out;
  wire [31:0] alu_1_aluout, bit_extender_1_out, data_memory_1_read_data, instruction_memory_1_instruction,
       multiplexer_2_out, multiplexer_5_out, register_file_1_read_data_1, register_file_1_read_data_2,
       shifter_2_out;

  Register #(.width(26)) PC (.D(multiplexer_4_out), .Q(PC_q), .clk(clock_1_out));  // open: en, clr
  Clock clock_1 (.out(clock_1_out));
  Instruction_Memory instruction_memory_1 (.Read_Address(PC_q), .Instruction(instruction_memory_1_instruction));
  Adder #(.width(26)) adder_1 (.a(PC_q), .b(26'h4), .out(adder_1_out));  // open: cin, cout
  Main_Control main_control_1 (
    .Opcode(instruction_memory_1_instruction[31:26]), .RegDst(main_control_1_regdst),
    .ALUSrc(main_control_1_alusrc), .MemtoReg(main_control_1_memtoreg), .RegWrite(main_control_1_regwrite),
    .MemRead(main_control_1_memread), .MemWrite(main_control_1_memwrite), .Branch(main_control_1_branch),
    .ALUOp(main_control_1_aluop), .Jump(main_control_1_jump));
  Shifter #(.width(26)) shifter_1 (.in(instruction_memory_1_instruction[25:0]), .\dist (5'b00010), .out(shifter_1_out));
  Register_File register_file_1 (
    .RegWrite(main_control_1_regwrite), .Write_Register(multiplexer_1_out),
    .Read_Register_1(instruction_memory_1_instruction[25:21]),
    .Read_Register_2(instruction_memory_1_instruction[20:16]), .Read_Data_1(register_file_1_read_data_1),
    .Read_Data_2(register_file_1_read_data_2), .Clock(clock_1_out), .Write_Data(multiplexer_5_out));
  Multiplexer #(.width(5), .enable("false")) multiplexer_1 (
    .in0(instruction_memory_1_instruction[20:16]), .in1(instruction_memory_1_instruction[15:11]),
    .out(multiplexer_1_out), .sel(main_control_1_regdst));
  ALU_Control alu_control_1 (
    .ALUOp(main_control_1_aluop), .Function(instruction_memory_1_instruction[5:0]),
    .Operation(alu_control_1_operation));
  assign bit_extender_1_out = {{16{instruction_memory_1_instruction[15]}}, instruction_memory_1_instruction[15:0]};  // Bit_Extender bit_extender_1
  Shifter #(.width(32)) shifter_2 (.in(bit_extender_1_out), .\dist (5'b00010), .out(shifter_2_out));
  ALU alu_1 (
    .ALUin_1(register_file_1_read_data_1), .ALUin_2(multiplexer_2_out), .ALUout(alu_1_aluout),
    .Zero(alu_1_zero), .ALU_Operation(alu_control_1_operation));
  Multiplexer #(.width(32), .enable("false")) multiplexer_2 (
    .in0(register_file_1_read_data_2), .in1(bit_extender_1_out), .out(multiplexer_2_out),
    .sel(main_control_1_alusrc));
  Adder #(.width(26)) adder_2 (.a(adder_1_out), .b(shifter_2_out[25:0]), .out(adder_2_out));  // open: cin, cout
  Multiplexer #(.width(26), .enable("false")) multiplexer_3 (
    .in0(adder_1_out), .in1(adder_2_out), .out(multiplexer_3_out), .sel(and_1_out));
  not not_1 (not_1_out, main_control_1_jump);
  and and_1 (and_1_out, main_control_1_branch, alu_1_zero);
  Multiplexer #(.width(26), .enable("false")) multiplexer_4 (
    .in0(shifter_1_out), .in1(multiplexer_3_out), .out(multiplexer_4_out), .sel(not_1_out));
  Data_Memory data_memory_1 (
    .Address(alu_1_aluout[23:0]), .Write_Data(register_file_1_read_data_2), .Clock(clock_1_out),
    .MemRead(main_control_1_memread), .MemWrite(main_control_1_memwrite), .Read_Data(data_memory_1_read_data));
  not not_2 (not_2_out, main_control_1_memtoreg);
  Multiplexer #(.width(32), .enable("false")) multiplexer_5 (
    .in0(data_memory_1_read_data), .in1(alu_1_aluout), .out(multiplexer_5_out), .sel(not_2_out));
endmodule

module Register_File (
  input  [4:0] Read_Register_1,
  input  [4:0] Write_Register,
  input  [31:0] Write_Data,
  input  [4:0] Read_Register_2,
  input  RegWrite,
  input  Clock,
  output [31:0] Read_Data_1,
  output [31:0] Read_Data_2
);

  wire and_1_out, decoder_1_out0, decoder_1_out1, decoder_1_out2, decoder_1_out3, decoder_1_out4,
       decoder_1_out5, decoder_1_out6, decoder_1_out7, decoder_1_out8, decoder_1_out9, decoder_1_out10,
       decoder_1_out11, decoder_1_out12, decoder_1_out13, decoder_1_out14, decoder_1_out15, decoder_1_out16,
       decoder_1_out17, decoder_1_out18, decoder_1_out19, decoder_1_out20, decoder_1_out21, decoder_1_out22,
       decoder_1_out23, decoder_1_out24, decoder_1_out25, decoder_1_out26, decoder_1_out27, decoder_1_out28,
       decoder_1_out29, decoder_1_out30, decoder_1_out31;
  wire [31:0] r0_q, r1_q, r2_q, r3_q, r4_q, r5_q, r6_q, r7_q, r8_q, r9_q, r10_q, r11_q, r12_q, r13_q, r14_q,
       r15_q, r16_q, r17_q, r18_q, r19_q, r20_q, r21_q, r22_q, r23_q, r24_q, r25_q, r26_q, r27_q, r28_q,
       r29_q, r30_q, r31_q;

  Decoder #(.select(5), .enable("false")) decoder_1 (
    .out0(decoder_1_out0), .out1(decoder_1_out1), .out2(decoder_1_out2), .out3(decoder_1_out3),
    .out4(decoder_1_out4), .out5(decoder_1_out5), .out6(decoder_1_out6), .out7(decoder_1_out7),
    .out8(decoder_1_out8), .out9(decoder_1_out9), .out10(decoder_1_out10), .out11(decoder_1_out11),
    .out12(decoder_1_out12), .out13(decoder_1_out13), .out14(decoder_1_out14), .out15(decoder_1_out15),
    .out16(decoder_1_out16), .out17(decoder_1_out17), .out18(decoder_1_out18), .out19(decoder_1_out19),
    .out20(decoder_1_out20), .out21(decoder_1_out21), .out22(decoder_1_out22), .out23(decoder_1_out23),
    .out24(decoder_1_out24), .out25(decoder_1_out25), .out26(decoder_1_out26), .out27(decoder_1_out27),
    .out28(decoder_1_out28), .out29(decoder_1_out29), .out30(decoder_1_out30), .out31(decoder_1_out31),
    .sel(Write_Register));
  Register #(.width(32)) r28 (.D(Write_Data), .en(decoder_1_out28), .Q(r28_q), .clk(and_1_out));  // open: clr
  Register #(.width(32)) r29 (.D(Write_Data), .en(decoder_1_out29), .Q(r29_q), .clk(and_1_out));  // open: clr
  Register #(.width(32)) r30 (.D(Write_Data), .en(decoder_1_out30), .Q(r30_q), .clk(and_1_out));  // open: clr
  Register #(.width(32)) r31 (.D(Write_Data), .en(decoder_1_out31), .Q(r31_q), .clk(and_1_out));  // open: clr
  Register #(.width(32)) r24 (.D(Write_Data), .en(decoder_1_out24), .Q(r24_q), .clk(and_1_out));  // open: clr
  Register #(.width(32)) r25 (.D(Write_Data), .en(decoder_1_out25), .Q(r25_q), .clk(and_1_out));  // open: clr
  Register #(.width(32)) r26 (.D(Write_Data), .en(decoder_1_out26), .Q(r26_q), .clk(and_1_out));  // open: clr
  Register #(.width(32)) r27 (.D(Write_Data), .en(decoder_1_out27), .Q(r27_q), .clk(and_1_out));  // open: clr
  and and_1 (and_1_out, RegWrite, Clock);
  Register #(.width(32)) r20 (.D(Write_Data), .en(decoder_1_out20), .Q(r20_q), .clk(and_1_out));  // open: clr
  Register #(.width(32)) r21 (.D(Write_Data), .en(decoder_1_out21), .Q(r21_q), .clk(and_1_out));  // open: clr
  Register #(.width(32)) r22 (.D(Write_Data), .en(decoder_1_out22), .Q(r22_q), .clk(and_1_out));  // open: clr
  Register #(.width(32)) r23 (.D(Write_Data), .en(decoder_1_out23), .Q(r23_q), .clk(and_1_out));  // open: clr
  // Probe on r16_q
  Register #(.width(32)) r16 (.D(Write_Data), .en(decoder_1_out16), .Q(r16_q), .clk(and_1_out));  // open: clr
  Register #(.width(32)) r17 (.D(Write_Data), .en(decoder_1_out17), .Q(r17_q), .clk(and_1_out));  // open: clr
  Register #(.width(32)) r18 (.D(Write_Data), .en(decoder_1_out18), .Q(r18_q), .clk(and_1_out));  // open: clr
  Register #(.width(32)) r19 (.D(Write_Data), .en(decoder_1_out19), .Q(r19_q), .clk(and_1_out));  // open: clr
  Register #(.width(32)) r12 (.D(Write_Data), .en(decoder_1_out12), .Q(r12_q), .clk(and_1_out));  // open: clr
  Register #(.width(32)) r13 (.D(Write_Data), .en(decoder_1_out13), .Q(r13_q), .clk(and_1_out));  // open: clr
  Register #(.width(32)) r14 (.D(Write_Data), .en(decoder_1_out14), .Q(r14_q), .clk(and_1_out));  // open: clr
  Register #(.width(32)) r15 (.D(Write_Data), .en(decoder_1_out15), .Q(r15_q), .clk(and_1_out));  // open: clr
  Register #(.width(32)) r8 (.D(Write_Data), .en(decoder_1_out8), .Q(r8_q), .clk(and_1_out));  // open: clr
  Register #(.width(32)) r9 (.D(Write_Data), .en(decoder_1_out9), .Q(r9_q), .clk(and_1_out));  // open: clr
  Register #(.width(32)) r10 (.D(Write_Data), .en(decoder_1_out10), .Q(r10_q), .clk(and_1_out));  // open: clr
  Register #(.width(32)) r11 (.D(Write_Data), .en(decoder_1_out11), .Q(r11_q), .clk(and_1_out));  // open: clr
  Register #(.width(32)) r4 (.D(Write_Data), .en(decoder_1_out4), .Q(r4_q), .clk(and_1_out));  // open: clr
  Register #(.width(32)) r5 (.D(Write_Data), .en(decoder_1_out5), .Q(r5_q), .clk(and_1_out));  // open: clr
  Register #(.width(32)) r6 (.D(Write_Data), .en(decoder_1_out6), .Q(r6_q), .clk(and_1_out));  // open: clr
  Register #(.width(32)) r7 (.D(Write_Data), .en(decoder_1_out7), .Q(r7_q), .clk(and_1_out));  // open: clr
  Register #(.width(32)) r0 (.D({32{1'b0}}), .en(decoder_1_out0), .Q(r0_q), .clk(and_1_out));  // open: clr
  Register #(.width(32)) r1 (.D(Write_Data), .en(decoder_1_out1), .Q(r1_q), .clk(and_1_out));  // open: clr
  Register #(.width(32)) r2 (.D(Write_Data), .en(decoder_1_out2), .Q(r2_q), .clk(and_1_out));  // open: clr
  Register #(.width(32)) r3 (.D(Write_Data), .en(decoder_1_out3), .Q(r3_q), .clk(and_1_out));  // open: clr
  Multiplexer #(.select(5), .width(32), .enable("false")) multiplexer_1 (
    .in0(r0_q), .in1(r1_q), .in2(r2_q), .in3(r3_q), .in4(r4_q), .in5(r5_q), .in6(r6_q), .in7(r7_q),
    .in8(r8_q), .in9(r9_q), .in10(r10_q), .in11(r11_q), .in12(r12_q), .in13(r13_q), .in14(r14_q),
    .in15(r15_q), .in16(r16_q), .in17(r17_q), .in18(r18_q), .in19(r19_q), .in20(r20_q), .in21(r21_q),
    .in22(r22_q), .in23(r23_q), .in24(r24_q), .in25(r25_q), .in26(r26_q), .in27(r27_q), .in28(r28_q),
    .in29(r29_q), .in30(r30_q), .in31(r31_q), .out(Read_Data_1), .sel(Read_Register_1));
  Multiplexer #(.select(5), .width(32), .enable("false")) multiplexer_2 (
    .in0(r0_q), .in1(r1_q), .in2(r2_q), .in3(r3_q), .in4(r4_q), .in5(r5_q), .in6(r6_q), .in7(r7_q),
    .in8(r8_q), .in9(r9_q), .in10(r10_q), .in11(r11_q), .in12(r12_q), .in13(r13_q), .in14(r14_q),
    .in15(r15_q), .in16(r16_q), .in17(r17_q), .in18(r18_q), .in19(r19_q), .in20(r20_q), .in21(r21_q),
    .in22(r22_q), .in23(r23_q), .in24(r24_q), .in25(r25_q), .in26(r26_q), .in27(r27_q), .in28(r28_q),
    .in29(r29_q), .in30(r30_q), .in31(r31_q), .out(Read_Data_2), .sel(Read_Register_2));
endmodule

module ALU (
  input  [2:0] ALU_Operation,
  input  [31:0] ALUin_1,
  input  [31:0] ALUin_2,
  output Zero,
  output [31:0] ALUout
);

  wire [31:0] adder_1_out, and_1_out, or_1_out, subtractor_1_out;

  assign and_1_out = ALUin_1 & ALUin_2;  // AND_Gate and_1, 32 bits wide
  assign or_1_out = ALUin_1 | ALUin_2;  // OR_Gate or_1, 32 bits wide
  Adder #(.width(32)) adder_1 (.a(ALUin_1), .b(ALUin_2), .out(adder_1_out));  // open: cin, cout
  Subtractor #(.width(32)) subtractor_1 (.a(ALUin_1), .b(ALUin_2), .out(subtractor_1_out));  // open: bin, bout
  Multiplexer #(.select(3), .width(32), .enable("false")) multiplexer_1 (
    .in0(and_1_out), .in1(or_1_out), .in2(adder_1_out), .in6(subtractor_1_out), .out(ALUout),
    .sel(ALU_Operation));  // open: in3, in4, in5, in7
  Comparator #(.width(32)) comparator_1 (.a({32{1'b0}}), .b(ALUout), .eq(Zero));  // open: gt, lt
endmodule

module Instruction_Memory (
  input  [25:0] Read_Address,
  output [31:0] Instruction
);

  wire [25:0] shifter_1_out;

  Shifter #(.width(26), .shift("lr")) shifter_1 (.in(Read_Address), .\dist (5'b00010), .out(shifter_1_out));
  ROM #(.addrWidth(24), .dataWidth(32)) rom_1 (.addr(shifter_1_out[23:0]), .data(Instruction));  // open: sel

  // Notes on the sheet:
  //   contents of rom_1 (hex, n*v repeats v):
  //   0 1285820 1286022 1286824 1287025 ac0b0000 ac0c0001 ac0d0002 ac0e0003 8c0f0001 11ec001f 15*0 8000000
  //   16*0 1f08020 8000019
endmodule

module Data_Memory (
  input  [31:0] Write_Data,
  input  [23:0] Address,
  input  Clock,
  input  MemRead,
  input  MemWrite,
  output [31:0] Read_Data
);

  wire multiplexer_1_out, xor_1_out;

  RAM #(.addrWidth(24), .dataWidth(32)) ram_1 (
    .addr(Address), .data(Read_Data), .clk(Clock), .ld(multiplexer_1_out));  // open: sel, clr
  Multiplexer multiplexer_1 (.in0(1'b0), .in1(1'b1), .out(multiplexer_1_out), .sel(MemRead), .en(xor_1_out));
  xor xor_1 (xor_1_out, MemRead, MemWrite);
  Multiplexer #(.width(32)) multiplexer_2 (
    .in0(Write_Data), .out(Read_Data), .sel(MemRead), .en(xor_1_out));  // open: in1
endmodule

module Main_Control (
  input  [5:0] Opcode,
  output RegDst,
  output ALUSrc,
  output MemtoReg,
  output RegWrite,
  output MemRead,
  output MemWrite,
  output Branch,
  output [1:0] ALUOp,
  output Jump
);

  wire not_1_out, not_2_out, not_3_out, not_4_out, not_5_out, not_6_out, not_7_out, not_8_out, not_9_out,
       not_10_out, not_11_out, not_12_out, not_13_out, not_14_out, not_15_out, not_16_out, not_17_out,
       not_18_out, not_19_out, not_20_out, not_21_out;

  not not_1 (not_1_out, Opcode[5]);
  not not_2 (not_2_out, Opcode[0]);
  not not_3 (not_3_out, Opcode[3]);
  not not_4 (not_4_out, Opcode[2]);
  not not_5 (not_5_out, Opcode[1]);
  not not_6 (not_6_out, Opcode[4]);
  and R_format (ALUOp[1], not_1_out, not_6_out, not_3_out, not_4_out, not_5_out, not_2_out);
  not not_7 (not_7_out, Opcode[2]);
  not not_8 (not_8_out, Opcode[3]);
  not not_9 (not_9_out, Opcode[4]);
  and lw (MemRead, Opcode[5], not_9_out, not_8_out, not_7_out, Opcode[1], Opcode[0]);
  not not_10 (not_10_out, Opcode[4]);
  not not_11 (not_11_out, Opcode[2]);
  and sw (MemWrite, Opcode[5], not_10_out, Opcode[3], not_11_out, Opcode[1], Opcode[0]);
  not not_12 (not_12_out, Opcode[4]);
  not not_13 (not_13_out, Opcode[5]);
  not not_14 (not_14_out, Opcode[3]);
  not not_15 (not_15_out, Opcode[1]);
  not not_16 (not_16_out, Opcode[5]);
  not not_17 (not_17_out, Opcode[0]);
  and beq (ALUOp[0], not_13_out, not_12_out, not_14_out, Opcode[2], not_15_out, not_17_out);
  not not_18 (not_18_out, Opcode[3]);
  not not_19 (not_19_out, Opcode[2]);
  not not_20 (not_20_out, Opcode[4]);
  not not_21 (not_21_out, Opcode[0]);
  and j (Jump, not_16_out, not_20_out, not_18_out, not_19_out, Opcode[1], not_21_out);
  or or_1 (ALUSrc, MemRead, MemWrite);
  or or_2 (RegWrite, MemRead, ALUOp[1]);

  assign Branch = ALUOp[0];
  assign MemtoReg = MemRead;
  assign RegDst = ALUOp[1];
endmodule

module ALU_Control (
  input  [1:0] ALUOp,
  input  [5:0] Function,
  output [2:0] Operation
);

  wire and_2_out, not_1_out, not_2_out, or_1_out;

  or or_1 (or_1_out, Function[3], Function[0]);
  and and_1 (Operation[0], ALUOp[1], or_1_out);
  and and_2 (and_2_out, ALUOp[1], Function[1]);
  or or_2 (Operation[2], ALUOp[0], and_2_out);
  not not_1 (not_1_out, ALUOp[1]);
  or or_3 (Operation[1], not_1_out, not_2_out);
  not not_2 (not_2_out, Function[2]);
endmodule
